# Fritzing sketch bluetoothControlledAC_Light (saved by Fritzing 0.9.3b)
breadboards: 1

parts:
  LED1 = LEDs [package=led10mm]
  U1 = 4-Channel 5v Relay Shield [package=relay-4ch5v10a]
  Part2 = Bluetooth HC-05 Macho
  U2 = BUTTONPAD-2X2SINGLE [package=buttonpad-2x2single-kit]
  Part1 = Arduino Uno (Rev3)
  LED2 = LEDs [package=led10mm]
  VCC1 = Battery

nets:
  N1: LED1.C, U1.K2-On
  VCC: U1.VCC, Part1.5V
  GND: U1.GND, Part2.GND, Part1.GND, VCC1.-, VCC1.+
  N2: U1.IN1, Part1.D8
  N3: U1.IN2, Part1.D9_PWM
  N4: U1.K1-Off, U2.C2_A
  N5: U1.K1-On, LED2.C
  N6: U1.K2-Off, U2.C2_SIG1
  N7: Part2.TXD, Part1.D0/RX
  N8: Part2.RXD, Part1.D1/TX

notes:
  AC Supply (220V~)
  Arduino Uno
  4 Channel Relay
  5V Battery
  Bluetooth
  Bread Board
  BULB-1
  BULB-2
  Switch-1
  Switch-2
  Positive Line
  Negative Line

custom parts:
  LEDs: LEDs Standard schematic elements and footprints for 5mm, 3mm, 1206, and 0603 sized LEDs. 5mm - Spark Fun Electronics SKU : COM-00529 (and others)
  4-Channel 5v Relay Shield: 4 Channel 5v Relay Shield w. 2x SPD-06VDC-SD-C
